// Logisim project BoothsAlgorithm.circ as structural Verilog: 1 circuit, main circuit main
module main (
);

  wire and_2_out, and_3_out, CLEAR, clock_1_out, counter_1_q, counter_2_q, not_1_out, not_2_out, not_3_out,
       or_1_out, SHIFT_ON, shift_register_1_out, shift_register_3_out, shift_register_3_q4, xor_1_out;
  wire [4:0] adder_1_out, multiplexer_1_out, shift_register_1_q4, shift_register_2_q4, subtractor_1_out;

  Clock clock_1 (.out(clock_1_out));
  // AND_Gate and_1 has open pins: in1=clock_1_out, out=open
  not not_1 (not_1_out, SHIFT_ON);
  Shift_Register #(.length(5)) shift_register_1 (
    .shift(SHIFT_ON), .in(shift_register_1_q4[4]), .clk(clock_1_out), .out(shift_register_1_out),
    .load(not_1_out), .clr(CLEAR), .d0(multiplexer_1_out[4]), .q0(shift_register_1_q4[4]),
    .d1(multiplexer_1_out[3]), .q1(shift_register_1_q4[3]), .d2(multiplexer_1_out[2]),
    .q2(shift_register_1_q4[2]), .d3(multiplexer_1_out[1]), .q3(shift_register_1_q4[1]),
    .d4(multiplexer_1_out[0]), .q4(shift_register_1_q4[0]));
  Shift_Register #(.length(5)) shift_register_2 (
    .clr(CLEAR), .q0(shift_register_2_q4[4]), .q1(shift_register_2_q4[3]), .q2(shift_register_2_q4[2]),
    .q3(shift_register_2_q4[1]), .q4(shift_register_2_q4[0]));  // open: shift, in, clk, out, load, d0, d1, d2, d3, d4
  Shift_Register #(.length(5)) shift_register_3 (
    .shift(SHIFT_ON), .in(shift_register_1_out), .clk(clock_1_out), .out(shift_register_3_out), .clr(CLEAR),
    .q4(shift_register_3_q4));  // open: load, d0, q0, d1, q1, d2, q2, d3, q3, d4
  Adder #(.width(5)) adder_1 (.a(shift_register_1_q4), .b(shift_register_2_q4), .out(adder_1_out));  // open: cin, cout
  Subtractor #(.width(5)) subtractor_1 (
    .a(shift_register_1_q4), .b(shift_register_2_q4), .out(subtractor_1_out));  // open: bin, bout
  Counter #(.width(1), .max('h1)) counter_1 (
    .load(SHIFT_ON), .D(shift_register_3_out), .count(1'b0), .Q(counter_1_q), .clk(clock_1_out), .clr(CLEAR));  // open: carry
  xor xor_1 (xor_1_out, shift_register_3_q4, counter_1_q);
  Multiplexer #(.width(5), .enable("false")) multiplexer_1 (
    .in0(adder_1_out), .in1(subtractor_1_out), .out(multiplexer_1_out), .sel(not_2_out));
  not not_2 (not_2_out, and_3_out);
  or or_1 (or_1_out, ~xor_1_out, counter_2_q);  // OR_Gate
  and and_2 (and_2_out, or_1_out, clock_1_out);
  not not_3 (not_3_out, xor_1_out);
  Counter #(.width(1), .max('h1), .trigger("falling")) counter_2 (
    .count(xor_1_out), .Q(counter_2_q), .clk(clock_1_out), .clr(CLEAR));  // open: load, D, carry
  Counter #(.width(3), .max('h5)) counter_3 (
    .load(1'b1), .count(1'b1), .carry(CLEAR), .clk(and_2_out));  // open: D, Q, clr
  or or_2 (SHIFT_ON, not_3_out, counter_2_q);
  and and_3 (and_3_out, counter_1_q, xor_1_out);

  // Notes on the sheet:
  //   BR
  //   A
  //   Q
  //   Qn+1
endmodule
