// Logisim project Control-Memory.circ as structural Verilog: 1 circuit, main circuit main
module main (
);

  wire and_3_out, and_4_out, CLK, decoder_1_out5, decoder_1_out6, LOAD_AC, LOAD_AR, LOAD_DR, LOAD_MEMORY,
       LOAD_SBR, not_2_out, not_4_out, or_2_out, or_4_out, PC_INC, SEL_MUX1, SEL_MUX2, TEST, Z;
  wire [0:0] SELECT;
  wire [1:0] BR;
  wire [2:0] F1, F2, F3;
  wire [6:0] adder_1_out, bit_extender_3_out, counter_1_q, counter_4_q;
  wire [10:0] counter_2_q, counter_3_q, multiplexer_2_out, ram_1_data, undriven;
  wire [15:0] AC, bit_extender_2_out, DR, multiplexer_3_out, ram_2_data, SUM;

  Clock clock_1 (.out(CLK));
  Multiplexer #(.select(2), .width(7), .enable("false")) multiplexer_1 (
    .in0(adder_1_out), .in1(bit_extender_3_out), .in2(counter_4_q), .in3({1'b0, DR[14:11], 2'b00}),
    .sel({BR[1], SELECT[0]}));  // open: out
  Counter #(.width(7), .max('h7f)) counter_1 (
    .D({1'b0, DR[14:11], 2'b00}), .count(1'b0), .Q(counter_1_q));  // open: load, carry, clk, clr
  Adder #(.width(7)) adder_1 (.a(counter_1_q), .b(7'b0000001), .out(adder_1_out));  // open: cin, cout
  Multiplexer #(.width(11), .enable("false")) multiplexer_2 (
    .in0(undriven), .in1(counter_3_q), .out(multiplexer_2_out), .sel(SEL_MUX1));
  Counter #(.width(11), .max('h7ff)) counter_2 (
    .load(LOAD_AR), .D(multiplexer_2_out), .count(1'b0), .Q(counter_2_q), .clk(CLK));  // open: carry, clr
  Counter #(.width(11), .max('h7ff)) counter_3 (
    .D(counter_2_q), .count(PC_INC), .Q(counter_3_q), .clk(CLK));  // open: load, carry, clr
  RAM #(.addrWidth(7), .dataWidth(20)) ram_1 (
    .addr(counter_1_q), .data({F3, F2, F1, ram_1_data[10:9], BR, ram_1_data[6:0]}));  // open: sel, clk, ld, clr
  Counter #(.width(7), .max('h7f)) counter_4 (
    .load(LOAD_SBR), .D(adder_1_out), .Q(counter_4_q));  // open: count, carry, clk, clr
  assign DR = {{5{1'b0}}, undriven};  // Bit_Extender bit_extender_1
  assign bit_extender_2_out = {{5{1'b0}}, counter_3_q};  // Bit_Extender bit_extender_2
  Decoder #(.select(3), .enable("false")) decoder_1 (
    .out1(LOAD_AC), .out5(decoder_1_out5), .out6(decoder_1_out6), .sel(F1));  // open: out0, out2, out3, out4, out7
  Multiplexer #(.select(2), .width(16), .enable("false")) multiplexer_3 (
    .in0(bit_extender_2_out), .in1(ram_2_data), .in2(AC), .out(multiplexer_3_out), .sel({1'b0, SEL_MUX2}));  // open: in3
  Counter #(.width(16), .max('hffff)) counter_5 (
    .load(LOAD_DR), .D(multiplexer_3_out), .count(1'b0), .Q(DR), .clk(CLK));  // open: carry, clr
  Counter #(.width(16), .max('hffff)) u_AC (
    .load(LOAD_AC), .D(SUM), .count(1'b0), .Q(AC), .clk(CLK));  // open: carry, clr
  Bit_Extender #(.in_width(20), .out_width(7)) bit_extender_3 (
    .in({F3, F2, F1, ram_1_data[10:9], BR, ram_1_data[6:0]}), .out(bit_extender_3_out));
  RAM #(.addrWidth(11), .dataWidth(16), .bus("separate")) ram_2 (
    .addr(counter_2_q), .data(ram_2_data), .clk(CLK), .ld(LOAD_MEMORY));  // open: din, str, sel, clr
  or or_1 (LOAD_AR, decoder_1_out6, decoder_1_out5);
  or or_2 (or_2_out, LOAD_MEMORY, decoder_1_out6);
  not not_1 (SEL_MUX1, LOAD_AR);
  Adder #(.width(16)) adder_2 (.a(AC), .b(DR), .out(SUM));  // open: cin, cout
  Decoder #(.select(3), .enable("false")) decoder_2 (
    .out4(LOAD_MEMORY), .sel(F2));  // open: out0, out1, out2, out3, out5, out6, out7
  Multiplexer #(.select(2), .enable("false")) multiplexer_4 (
    .in0(1'b1), .in1(DR[15]), .in2(AC[15]), .in3(Z), .out(TEST), .sel(ram_1_data[10:9]));
  or or_3 (LOAD_DR, LOAD_MEMORY, decoder_1_out6);
  and and_1 (SEL_MUX2, or_2_out, not_2_out);
  not not_2 (not_2_out, F2[1]);
  not not_3 (Z, or_4_out);
  or or_4 (or_4_out, AC[15], AC[14], AC[13], AC[12], AC[11], AC[10], AC[9], AC[8], AC[7], AC[6], AC[5], AC[4], AC[3], AC[2], AC[1], AC[0]);
  not not_4 (not_4_out, BR[1]);
  and and_2 (LOAD_SBR, TEST, BR[0], not_4_out);
  and and_3 (and_3_out, BR[1], BR[0]);
  and and_4 (and_4_out, not_4_out, TEST);
  or or_5 (SELECT[0], and_3_out, and_4_out);
  Decoder #(.select(3), .enable("false")) decoder_3 (
    .out5(PC_INC), .sel(F3));  // open: out0, out1, out2, out3, out4, out6, out7

  // Other names for the same wires on the sheet: S = AC[15]; I = DR[15]; MAP[5:2] = DR[14:11]; SELECT[1] = BR[1]

  // Notes on the sheet:
  //   CLOCK
  //   DR(15
  //   Mapping
  //   Control Unit
  //   CAR
  //   Microprogrammed Control Unit
  //   AR
  //   PC
  //   Control Memory
  //   SBR
  //   Memory
  //   DR
  //   AC
  //   F1
  //   DRTAR
  //   ADD
  //   PCTAR
  //   ALU
  //   Megh Patel
  //   16BIT020
  //   I0
  //   I1
  //   F2
  //   Input Logic
  //   READ
  //   MUX To Select Condition Bit
  //   S1 S0
  //   F3
  //   INCPC
endmodule
