// Logisim project PriorityEncoder.circ as structural Verilog: 1 circuit, main circuit main
module main (
  input  I0,
  input  I1,
  input  I2,
  input  I3,
  output O_1,
  output O_0
);

  wire and_1_out, not_1_out;

  or or_1 (O_1, I2, I3);
  not not_1 (not_1_out, I2);
  and and_1 (and_1_out, I1, not_1_out);
  or or_2 (O_0, and_1_out, I3);
endmodule
