// Logisim project Stack.circ as structural Verilog: 1 circuit, main circuit main
module main (
  input  [1:0] in_1,
  input  [1:0] PUSH,
  input  in_3,
  input  in_4,
  input  POP,
  output [1:0] out_6
);

  wire clock_1_out, or_1_out;
  wire [1:0] multiplexer_1_out;
  wire [7:0] counter_1_q;

  Multiplexer #(.width(2), .enable("false")) multiplexer_1 (
    .in0(in_1), .in1(PUSH), .out(multiplexer_1_out), .sel(in_3));
  or or_1 (or_1_out, POP, in_3);
  Clock clock_1 (.out(clock_1_out));
  Counter #(.ongoal("stay")) counter_1 (
    .load(POP), .count(or_1_out), .Q(counter_1_q), .clk(clock_1_out));  // open: D, carry, clr
  RAM #(.dataWidth(2), .bus("separate")) ram_1 (
    .addr(counter_1_q), .din(multiplexer_1_out), .data(out_6), .str(in_4), .clk(clock_1_out));  // open: sel, ld, clr

  // Notes on the sheet:
  //   Stack Operations
  //   Megh Patel
  //   16BIT020
endmodule
